# Fritzing sketch Untitled Sketch (saved by Fritzing 0.9.3b)
breadboards: 1

parts:
  hc-sr1 = hc-sr04
  J1 = Infrared Proximity Sensor
  Grove1 = Grove OLED 128x96
  Part1 = Arduino Uno (Rev3)

nets:
  VCC: hc-sr1.VCC, J1.Vcc, Grove1.VCC
  N1: hc-sr1.Trig, Part1.D6_PWM
  N2: hc-sr1.Echo, Part1.D5_PWM
  GND: hc-sr1.GND, J1.GND, Grove1.GND
  N3: J1.Vout, Part1.A3
  N4: Grove1.SDA, Part1.A4/SDA
  N5: Grove1.SCL, Part1.A5/SCL
